# Fritzing sketch frdmkl25 (saved by Fritzing 0.9.3b)
breadboards: 1

parts:
  FRDM-KL25Z1 = FRDM-KL25Z [part_number=FRDM-KL25Z]
  LED1 = LED - 5mm [color="Red (633nm)" package="5 mm [THT]"]
  LED2 = LED - 5mm [color="Red (633nm)" package="5 mm [THT]"]
  R1 = Resistor [tolerance=±5% resistance=220 package=THT]
  R2 = Resistor [tolerance=±5% resistance=220 package=THT]
  S1 = Pushbutton [package="[THT]"]
  R3 = Resistor [tolerance=±5% resistance=1k package=THT]
  S2 = Pushbutton [package="[THT]"]
  R4 = Resistor [tolerance=±5% resistance=1k package=THT]
  C1 = Electrolytic Capacitor [capacitance=1µF package="100 mil [THT, electrolytic]"]
  C2 = Electrolytic Capacitor [capacitance=1µF package="100 mil [THT, electrolytic]"]

nets:
  N1: FRDM-KL25Z1.D0_PTA1, LED2.anode
  N2: FRDM-KL25Z1.D2_PTD4, S1.Pin_3, S1.Pin_4, R3.Pin_0, C1.+
  N3: FRDM-KL25Z1.D3_PTA12_PWM, S2.Pin_3, S2.Pin_4, R4.Pin_0, C2.+
  N4: FRDM-KL25Z1.D8_PTA13, LED1.anode
  GND2: FRDM-KL25Z1.GND2, FRDM-KL25Z1.GND3, R1.Pin_1, R2.Pin_1, R3.Pin_1, R4.Pin_1, C1.-, C2.-
  N5: FRDM-KL25Z1.5V_P5V_USB, S1.Pin_1, S1.Pin_2, S2.Pin_1, S2.Pin_2
  N6: LED1.cathode, R1.Pin_0
  N7: LED2.cathode, R2.Pin_0

custom parts:
  FRDM-KL25Z: Freedom Board, based on basic pinout of Arduino Rev.3. Attention: the board is NOT 5V compatible.
